# Fritzing sketch motor (saved by Fritzing 0.9.3b)
breadboards: 1

parts:
  IC2 = L293D [package=THT]
  U1 = Voltage Regulator - 5V [package="TO220 [THT]"]
  M1 = DC Motor
  LCD1 = LCD screen
  R1 = Trimmer Potentiometer [maximum_resistance=10kΩ package=THT]
  Componente1 = Arduino Uno (Rev3)
  Componente2 = Bluetooth HC-05 Macho

nets:
  N1: IC2.Enable_1, Componente1.D9_PWM
  N2: IC2.Out_1_(_Controlled_by_Enable_1_), M1.pin_2
  GND: IC2.0V, U1.GND, LCD1.VSS, LCD1.LED-, R1.leg2
  N3: IC2.Out_2_(_Controlled_by_Enable_1_), M1.pin_1
  N4: IC2.+Vmotor, U1.input_voltage, Componente1.D11_PWM/MOSI
  N5: IC2.+V, U1.output_voltage, LCD1.VDD, LCD1.LED+, R1.leg1
  N6: LCD1.V0, R1.wiper
  N7: LCD1.RS, Componente1.D6_PWM
  N8: LCD1.DB0, Componente1.D7
  N9: LCD1.DB4, Componente1.D5_PWM
  N10: LCD1.DB5, Componente1.D4
  N11: LCD1.DB6, Componente1.D3_PWM
  N12: LCD1.DB7, Componente1.D2
  N13: Componente1.D0/RX, Componente2.TXD
  N14: Componente1.D1/TX, Componente2.RXD
  5V: Componente1.5V, Componente2.VCC
  GND_2: Componente1.GND, Componente2.GND
